# Fritzing sketch HDT11_attiny85 (saved by Fritzing 0.9.3b)
breadboards: 1

parts:
  U1 = attiny85 [package=dip]
  R1 = PHOTOCELL [package=photocell-kit]
  DHT1 = DHT11 Humitidy and Temperature Sensor
  J1 = Piezo Speaker
  Q1 = TRANSISTOR_NPN [package=to-92-ammo]
  Q2 = TRANSISTOR_NPN [package=to-92-ammo]
  LCD2 = LCD screen
  LCM1602_IIC2 = LCM1602 IIC [part_number="LCM1602 IIC" chip_label="LCM1602 IIC" package="DIP (Dual Inline) [THT]"]
  S1 = Momentary Switch [package=ksa_sealed_tac_switch]
  R2 = Resistor [tolerance=±5% resistance=220 package="1206 [SMD]"]

nets (from the breadboard view):
  N1: U1.Pin_1, S1.1, S1.2
  N2: U1.Pin_2, R2.Pin_1
  N3: U1.Pin_3, DHT1.DATA
  N4: U1.Pin_4, DHT1.GND, J1.pin1, Q1.E, S1.3, S1.4
  N5: U1.Pin_5, LCM1602_IIC2.SDA
  N6: U1.Pin_6, J1.pin2
  N7: U1.Pin_7, LCM1602_IIC2.SCL
  VDD: U1.Pin_8, R1.P$1, DHT1.VDD, LCM1602_IIC2.VCC
  N8: R1.P$2, Q2.B
  N9: Q1.B, R2.Pin_0
  N10: Q1.C, LCM1602_IIC2.GND
  N11: Q2.E, LCM1602_IIC2.LED_A
  N12: Q2.C, LCM1602_IIC2.LED_B
  VSS: LCD2.VSS, LCM1602_IIC2.VSS
  VDD_2: LCD2.VDD, LCM1602_IIC2.VDD
  N13: LCD2.V0, LCM1602_IIC2.V0
  N14: LCD2.RS, LCM1602_IIC2.RS
  N15: LCD2.R/W, LCM1602_IIC2.RW
  N16: LCD2.E, LCM1602_IIC2.E
  N17: LCD2.DB0, LCM1602_IIC2.D0
  N18: LCD2.DB1, LCM1602_IIC2.D1
  N19: LCD2.DB2, LCM1602_IIC2.D2
  N20: LCD2.DB3, LCM1602_IIC2.D3
  N21: LCD2.DB4, LCM1602_IIC2.D4
  N22: LCD2.DB5, LCM1602_IIC2.D5
  N23: LCD2.DB6, LCM1602_IIC2.D6
  N24: LCD2.DB7, LCM1602_IIC2.D7
  N25: LCD2.LED+, LCM1602_IIC2.A
  N26: LCD2.LED-, LCM1602_IIC2.K

custom parts:
  DHT11 Humitidy and Temperature Sensor: DHT11 Humidity and Temperature Sensor
  LCM1602 IIC: I2C-Module to use a 1602 or 2004 LCD on with the wire.h libory Serial LCD Modul
